// Logisim project Q1.circ as structural Verilog: 3 circuits, main circuit cir1
module cir1 (
  input  a0,
  input  a1,
  input  a2,
  input  a3,
  input  [3:0] b,
  output [2:0] c
);

  wire and_1_out, and_2_out, and_3_out, and_4_out, and_5_out, and_6_out, not_1_out, xor_1_out, xor_2_out,
       xor_3_out;

  not not_1 (not_1_out, a3);
  and and_1 (and_1_out, a3, b[0]);
  and and_2 (and_2_out, a3, b[1]);
  and and_3 (and_3_out, a3, b[2]);
  and and_4 (and_4_out, a0, not_1_out);
  and and_5 (and_5_out, a1, not_1_out);
  and and_6 (and_6_out, a2, not_1_out);
  xor xor_1 (xor_1_out, a0, and_1_out);
  xor xor_2 (xor_2_out, a1, and_2_out);
  xor xor_3 (xor_3_out, a2, and_3_out);
  or or_1 (c[0], and_4_out, xor_1_out);
  or or_2 (c[1], and_5_out, xor_2_out);
  or or_3 (c[2], and_6_out, xor_3_out);
endmodule

module CRC (
  input  [7:0] A,
  input  [3:0] B,
  output [10:0] C
);

  wire [2:0] cie_1_1_out_3, cir1_1_c, cir1_2_c, cir1_3_c, cir1_4_c, cir1_5_c, cir1_6_c;

  cie_1 cie_1_1 (.a(A[7:4]), .b(B), .out_3(cie_1_1_out_3));
  cir1 cir1_1 (.a0(A[3]), .a1(cie_1_1_out_3[0]), .a2(cie_1_1_out_3[1]), .a3(cie_1_1_out_3[2]), .b(B), .c(cir1_1_c));
  cir1 cir1_2 (.a0(A[2]), .a1(cir1_1_c[0]), .a2(cir1_1_c[1]), .a3(cir1_1_c[2]), .b(B), .c(cir1_2_c));
  cir1 cir1_3 (.a0(A[1]), .a1(cir1_2_c[0]), .a2(cir1_2_c[1]), .a3(cir1_2_c[2]), .b(B), .c(cir1_3_c));
  cir1 cir1_4 (.a0(A[0]), .a1(cir1_3_c[0]), .a2(cir1_3_c[1]), .a3(cir1_3_c[2]), .b(B), .c(cir1_4_c));
  cir1 cir1_5 (.a0(1'b0), .a1(cir1_4_c[0]), .a2(cir1_4_c[1]), .a3(cir1_4_c[2]), .b(B), .c(cir1_5_c));
  cir1 cir1_6 (.a0(1'b0), .a1(cir1_5_c[0]), .a2(cir1_5_c[1]), .a3(cir1_5_c[2]), .b(B), .c(cir1_6_c));
  cir1 cir1_7 (.a0(1'b0), .a1(cir1_6_c[0]), .a2(cir1_6_c[1]), .a3(cir1_6_c[2]), .b(B), .c(C[2:0]));

  assign C[10:3] = A;
endmodule

module cie_1 (
  input  [3:0] a,
  input  [3:0] b,
  output [2:0] out_3
);

  wire [2:0] bit_extender_1_out, xor_1_out;

  Bit_Extender #(.in_width(4), .out_width(3)) bit_extender_1 (.in(b), .out(bit_extender_1_out));
  assign xor_1_out = a[2:0] ^ bit_extender_1_out;  // XOR_Gate xor_1, 3 bits wide
  Multiplexer #(.width(3)) multiplexer_1 (.in0(a[2:0]), .in1(xor_1_out), .out(out_3), .sel(a[3]));  // open: en
endmodule
