// Logisim project Q2.circ as structural Verilog: 7 circuits, main circuit jia
module jia (
  input  [3:0] a,
  input  [3:0] b,
  output c0,
  output c1,
  output c2,
  output c3
);

  wire c11_out, c12_out, c21_out, c22_out, c31_out, c32_out, d1_out, d2_out, d3_out, d21_out, d22_out,
       d31_out, d32_out, not_1_out, not_2_out, not_3_out, or_1_out, or_2_out, xnor_1_out, xnor_2_out,
       xnor_3_out, xor_2_out, xor_3_out, xor_4_out;

  and d1 (d1_out, a[0], b[0]);
  xor xor_1 (c0, a[0], b[0]);
  not not_1 (not_1_out, d1_out);
  or or_1 (or_1_out, a[1], b[1]);
  and c11 (c11_out, not_1_out, xor_2_out);
  xor xor_2 (xor_2_out, a[1], b[1]);
  and d21 (d21_out, not_1_out, a[1], b[1]);
  and c12 (c12_out, d1_out, xnor_1_out);
  xnor xnor_1 (xnor_1_out, a[1], b[1]);
  and d22 (d22_out, d1_out, or_1_out);
  or u_c1 (c1, c11_out, c12_out);
  or d2 (d2_out, d21_out, d22_out);
  not not_2 (not_2_out, d2_out);
  xnor xnor_2 (xnor_2_out, a[2], b[2]);
  or or_2 (or_2_out, a[2], b[2]);
  xor xor_3 (xor_3_out, a[2], b[2]);
  and c21 (c21_out, not_2_out, xor_3_out);
  and d31 (d31_out, not_2_out, a[2], b[2]);
  and c22 (c22_out, d2_out, xnor_2_out);
  or d3 (d3_out, d31_out, d32_out);
  and d32 (d32_out, d2_out, or_2_out);
  xnor xnor_3 (xnor_3_out, a[3], b[3]);
  or u_c2 (c2, c21_out, c22_out);
  not not_3 (not_3_out, d3_out);
  xor xor_4 (xor_4_out, a[3], b[3]);
  and c31 (c31_out, not_3_out, xor_4_out);
  and c32 (c32_out, d3_out, xnor_3_out);
  or or_3 (c3, c31_out, c32_out);
endmodule

module jian (
  input  [3:0] a,
  input  [3:0] b,
  output out_3,
  output out_4,
  output out_5,
  output out_6
);

  wire [3:0] jia_1_c0, not_1_out;

  not not_1 (not_1_out[0], b[0]);
  not not_2 (not_1_out[1], b[1]);
  not not_3 (not_1_out[2], b[2]);
  not not_4 (not_1_out[3], b[3]);
  jia jia_1 (.a(not_1_out), .b(4'b0001), .c0(jia_1_c0[0]), .c1(jia_1_c0[1]), .c2(jia_1_c0[2]), .c3(jia_1_c0[3]));
  jia jia_2 (.a(a), .b(jia_1_c0), .c0(out_3), .c1(out_4), .c2(out_5), .c3(out_6));
endmodule

module yu (
  input  [3:0] a,
  input  [3:0] b,
  output c0,
  output c1,
  output c2,
  output c3
);

  and and_1 (c0, a[0], b[0]);
  and and_2 (c1, a[1], b[1]);
  and and_3 (c2, a[2], b[2]);
  and and_4 (c3, a[3], b[3]);
endmodule

module huo (
  input  [3:0] a,
  input  [3:0] b,
  output c0,
  output c1,
  output c2,
  output c3
);

  or or_1 (c0, a[0], b[0]);
  or or_2 (c1, a[1], b[1]);
  or or_3 (c2, a[2], b[2]);
  or or_4 (c3, a[3], b[3]);
endmodule

module alu1 (
  input  [3:0] A,
  input  [3:0] B,
  input  [1:0] ALUOp,
  output [3:0] C
);

  wire and_1_out, and_2_out, and_3_out, and_4_out, and_5_out, and_6_out, and_7_out, and_8_out, and_9_out,
       and_10_out, and_11_out, and_12_out, and_13_out, and_14_out, and_15_out, and_16_out, huo_1_c0,
       huo_1_c1, huo_1_c2, huo_1_c3, jia_1_c0, jia_1_c1, jia_1_c2, jia_1_c3, jian_1_out_3, jian_1_out_4,
       jian_1_out_5, jian_1_out_6, not_1_out, not_2_out, yu_1_c0, yu_1_c1, yu_1_c2, yu_1_c3;

  jia jia_1 (.a(A), .b(B), .c0(jia_1_c0), .c1(jia_1_c1), .c2(jia_1_c2), .c3(jia_1_c3));
  jian jian_1 (.a(A), .b(B), .out_3(jian_1_out_3), .out_4(jian_1_out_4), .out_5(jian_1_out_5), .out_6(jian_1_out_6));
  yu yu_1 (.a(A), .b(B), .c0(yu_1_c0), .c1(yu_1_c1), .c2(yu_1_c2), .c3(yu_1_c3));
  huo huo_1 (.a(A), .b(B), .c0(huo_1_c0), .c1(huo_1_c1), .c2(huo_1_c2), .c3(huo_1_c3));
  not not_1 (not_1_out, ALUOp[1]);
  and and_1 (and_1_out, jia_1_c0, not_1_out, not_2_out);
  and and_2 (and_2_out, jian_1_out_3, not_1_out, ALUOp[0]);
  and and_3 (and_3_out, yu_1_c0, ALUOp[1], not_2_out);
  not not_2 (not_2_out, ALUOp[0]);
  and and_4 (and_4_out, huo_1_c0, ALUOp[1], ALUOp[0]);
  and and_5 (and_5_out, jia_1_c2, not_1_out, not_2_out);
  and and_6 (and_6_out, jian_1_out_5, not_1_out, ALUOp[0]);
  and and_7 (and_7_out, yu_1_c2, ALUOp[1], not_2_out);
  and and_8 (and_8_out, huo_1_c2, ALUOp[1], ALUOp[0]);
  and and_9 (and_9_out, jia_1_c3, not_1_out, not_2_out);
  and and_10 (and_10_out, jian_1_out_6, not_1_out, ALUOp[0]);
  and and_11 (and_11_out, yu_1_c3, ALUOp[1], not_2_out);
  and and_12 (and_12_out, huo_1_c3, ALUOp[0], ALUOp[1]);
  and and_13 (and_13_out, jia_1_c1, not_1_out, not_2_out);
  and and_14 (and_14_out, jian_1_out_4, not_1_out, ALUOp[0]);
  and and_15 (and_15_out, yu_1_c1, ALUOp[1], not_2_out);
  and and_16 (and_16_out, huo_1_c1, ALUOp[1], ALUOp[0]);
  or or_1 (C[0], and_1_out, and_2_out, and_3_out, and_4_out);
  or or_2 (C[1], and_13_out, and_14_out, and_15_out, and_16_out);
  or or_3 (C[2], and_5_out, and_6_out, and_7_out, and_8_out);
  or or_4 (C[3], and_9_out, and_10_out, and_11_out, and_12_out);
endmodule

module alu (
  input  [3:0] A,
  input  [3:0] B,
  input  [1:0] ALUOp,
  output [3:0] C
);

  wire [3:0] huo_1_c0, jia_1_c0, jian_1_out_3, yu_1_c0;

  jia jia_1 (.a(A), .b(B), .c0(jia_1_c0[0]), .c1(jia_1_c0[1]), .c2(jia_1_c0[2]), .c3(jia_1_c0[3]));
  jian jian_1 (
    .a(A), .b(B), .out_3(jian_1_out_3[0]), .out_4(jian_1_out_3[1]), .out_5(jian_1_out_3[2]),
    .out_6(jian_1_out_3[3]));
  yu yu_1 (.a(A), .b(B), .c0(yu_1_c0[0]), .c1(yu_1_c0[1]), .c2(yu_1_c0[2]), .c3(yu_1_c0[3]));
  huo huo_1 (.a(A), .b(B), .c0(huo_1_c0[0]), .c1(huo_1_c0[1]), .c2(huo_1_c0[2]), .c3(huo_1_c0[3]));
  Multiplexer #(.select(2), .width(4)) multiplexer_1 (
    .in0(jia_1_c0), .in1(jian_1_out_3), .in2(yu_1_c0), .in3(huo_1_c0), .out(C), .sel(ALUOp));  // open: en
endmodule

module alu_up (
  input  [3:0] a,
  input  [3:0] b,
  input  [1:0] in_3,
  output [3:0] out_4
);

  wire [3:0] adder_1_out, and_1_out, or_1_out, subtractor_1_out;

  Adder #(.width(4)) adder_1 (.a(a), .b(b), .out(adder_1_out));  // open: cin, cout
  Subtractor #(.width(4)) subtractor_1 (.a(a), .b(b), .out(subtractor_1_out));  // open: bin, bout
  assign and_1_out = a & b;  // AND_Gate and_1, 4 bits wide
  assign or_1_out = a | b;  // OR_Gate or_1, 4 bits wide
  Multiplexer #(.select(2), .width(4)) multiplexer_1 (
    .in0(adder_1_out), .in1(subtractor_1_out), .in2(and_1_out), .in3(or_1_out), .out(out_4), .sel(in_3));  // open: en
endmodule
