// Logisim project Q3.circ as structural Verilog: 5 circuits, main circuit shuchu
module shuchu (
  input  in0,
  input  s1,
  input  s0,
  output z
);

  wire and_1_out, and_2_out, not_1_out;

  not not_1 (not_1_out, in0);
  and and_1 (and_1_out, not_1_out, s1);
  and and_2 (and_2_out, s1, s0);
  or or_1 (z, and_1_out, and_2_out);
endmodule

module citai (
  input  s0,
  input  in1,
  input  in0,
  output _s1,
  output _s0
);

  wire not_1_out, not_2_out;

  and and_1 (_s1, s0, not_1_out);
  not not_1 (not_1_out, in0);
  not not_2 (not_2_out, in1);
  and and_2 (_s0, not_2_out, in0);
endmodule

module fsm (
  input  [1:0] In,
  input  CLR,
  input  [1:0] in_2,
  input  clr_2,
  output Z,
  output out_6
);

  wire and_1_out, clock_1_out, clock_2_out, register_2_q;
  wire [1:0] citai1_1__s0, citai1_2__s0, multiplexer_1_out, register_1_q, register_3_q;

  Register #(.width(2)) register_1 (
    .D(citai1_1__s0), .Q(register_1_q), .clk(clock_1_out), .clr(and_1_out));  // open: en
  Clock clock_1 (.out(clock_1_out));
  and and_1 (and_1_out, CLR, register_2_q);
  Register #(.width(1)) register_2 (.D(CLR), .Q(register_2_q), .clk(clock_1_out));  // open: en, clr
  citai1 citai1_1 (
    .s1(register_1_q[1]), .s0(register_1_q[0]), .in1(In[1]), .in0(In[0]), ._s1(citai1_1__s0[1]),
    ._s0(citai1_1__s0[0]), .z(Z));
  citai1 citai1_2 (
    .s1(register_3_q[1]), .s0(register_3_q[0]), .in1(in_2[1]), .in0(in_2[0]), ._s1(citai1_2__s0[1]),
    ._s0(citai1_2__s0[0]), .z(out_6));
  Multiplexer #(.width(2)) multiplexer_1 (
    .in0(citai1_2__s0), .in1(2'b00), .out(multiplexer_1_out), .sel(clr_2));  // open: en
  Register #(.width(2)) register_3 (.D(multiplexer_1_out), .Q(register_3_q), .clk(clock_2_out));  // open: en, clr
  Clock clock_2 (.out(clock_2_out));
endmodule

module shuchu1 (
  input  s1,
  input  in0,
  output d
);

  wire not_1_out;

  and and_1 (d, s1, not_1_out);
  not not_1 (not_1_out, in0);
endmodule

module citai1 (
  input  s1,
  input  s0,
  input  in1,
  input  in0,
  output _s1,
  output _s0,
  output z
);

  wire not_1_out, not_2_out, not_3_out;

  and and_1 (_s1, s0, not_1_out);
  not not_1 (not_1_out, in0);
  not not_2 (not_2_out, in1);
  and and_2 (_s0, not_2_out, in0);
  and and_3 (z, s1, not_3_out);
  not not_3 (not_3_out, in0);
endmodule
