// Logisim project single_cpu1.circ as structural Verilog: 10 circuits, main circuit main
module main (
  input  Reset,
  output [31:0] Instr,
  output RegWrite,
  output [4:0] RegAddr,
  output [31:0] RegData,
  output MemWrite,
  output [4:0] MemAddr,
  output [31:0] MemData
);

  wire ALU_zero, ALUSrc, clk, control_npc_sel, ExtOp, IFU_ins0, IFU_ins1, IFU_op0, IFU_op1, IFU_op2, IFU_op3,
       IFU_op4, IFU_op5, MemtoReg, PCSrc, RegDst;
  wire [1:0] ALUctr;
  wire [4:0] in_11_15, in_16_20, in_21_25;
  wire [15:0] imm;
  wire [29:0] multiplexer_1_out, PCBranch, PLUS1, register_1_q, shift_2_1_out_2;
  wire [31:0] ALU_aluresult, DM_readdata, EXT_ext_num, GRF_rd1, multiplexer_2_out;

  Multiplexer #(.width(30)) multiplexer_1 (
    .in0(PLUS1), .in1(PCBranch), .out(multiplexer_1_out), .sel(PCSrc));  // open: en
  Adder #(.width(30)) adder_1 (.a(register_1_q), .b(30'h1), .out(PLUS1));  // open: cin, cout
  Clock clock_1 (.out(clk));
  Register #(.width(30)) register_1 (.D(multiplexer_1_out), .Q(register_1_q), .clk(clk), .clr(Reset));  // open: en
  IFU IFU (
    .PC(register_1_q), .instruction(Instr), .ins0(IFU_ins0), .ins1(IFU_ins1), .op0(IFU_op0), .op1(IFU_op1),
    .op2(IFU_op2), .op3(IFU_op3), .op4(IFU_op4), .op5(IFU_op5), .in_21_25(in_21_25), .in_16_20(in_16_20),
    .in_11_15(in_11_15), .imm(imm));
  control control (
    .ALUctr1(ALUctr[1]), .ALUctr0(ALUctr[0]), .op5(IFU_op5), .op4(IFU_op4), .op3(IFU_op3), .op2(IFU_op2),
    .op1(IFU_op1), .op0(IFU_op0), .ins1(IFU_ins1), .RegDst(RegDst), .ALUSrc(ALUSrc), .MemtoReg(MemtoReg),
    .RegWrite(RegWrite), .Memwrite(MemWrite), .nPC_sel(control_npc_sel), .ExtOp(ExtOp), .ins0(IFU_ins0));
  EXT EXT (.ExtOp(ExtOp), .imm(imm), .Ext_num(EXT_ext_num));
  GPR GRF (
    .CLK(clk), .ALUSrc(ALUSrc), .RegDst(RegDst), .A1(in_21_25), .A2(in_16_20), .ins15_11(in_11_15),
    .WD3(RegData), .RegWrite(RegWrite), .in_9(Reset), .RD1(GRF_rd1), .RD2(MemData), .out_12(RegAddr));
  Multiplexer #(.width(32)) multiplexer_2 (
    .in0(MemData), .in1(EXT_ext_num), .out(multiplexer_2_out), .sel(ALUSrc));  // open: en
  shift_2 shift_2_1 (.in_1(EXT_ext_num), .out_2(shift_2_1_out_2));
  and and_1 (PCSrc, control_npc_sel, ALU_zero);
  ALU ALU (.ALUctr(ALUctr), .SrcA(GRF_rd1), .SrcB(multiplexer_2_out), .ZERO(ALU_zero), .ALUResult(ALU_aluresult));
  Adder #(.width(30)) adder_2 (.a(shift_2_1_out_2), .b(PLUS1), .out(PCBranch));  // open: cin, cout
  DM DM (
    .MemWrite(MemWrite), .ALUResult(ALU_aluresult), .WriteData(MemData), .ReadData(DM_readdata), .CLK(clk),
    .reset(Reset), .MemAddr(MemAddr));
  Multiplexer #(.width(32)) multiplexer_3 (
    .in0(ALU_aluresult), .in1(DM_readdata), .out(RegData), .sel(MemtoReg));  // open: en
endmodule

module IFU (
  input  [29:0] PC,
  output [31:0] instruction,
  output ins0,
  output ins1,
  output op0,
  output op1,
  output op2,
  output op3,
  output op4,
  output op5,
  output [4:0] in_21_25,
  output [4:0] in_16_20,
  output [4:0] in_11_15,
  output [15:0] imm
);

  ROM #(.addrWidth(5), .dataWidth(32)) rom_1 (
    .addr(PC[4:0]), .data({instruction[31:26], in_21_25, in_16_20, imm}));  // open: sel

  assign in_11_15 = imm[15:11];
  assign ins0 = imm[0];
  assign ins1 = imm[1];
  assign instruction[25:0] = {in_21_25, in_16_20, imm};
  assign op0 = instruction[26];
  assign op1 = instruction[27];
  assign op2 = instruction[28];
  assign op3 = instruction[29];
  assign op4 = instruction[30];
  assign op5 = instruction[31];

  // Notes on the sheet:
  //   contents of rom_1 (hex, n*v repeats v):
  //   36fa0002 34420001 0 ac1a0008 8c060008 431821 622023 3c050001 0 1062fffb
endmodule

module GPR (
  input  CLK,
  input  ALUSrc,
  input  RegDst,
  input  [4:0] A1,
  input  [4:0] A2,
  input  [4:0] ins15_11,
  input  [31:0] WD3,
  input  RegWrite,
  input  in_9,
  output [31:0] RD1,
  output [31:0] RD2,
  output [4:0] out_12
);

  wire demultiplexer_1_out0, P1, P2, P3, P4, P5, P6, P7, P8, P9, P10, P11, P12, P13, P14, P15, P16, P17, P18,
       P19, P20, P21, P22, P23, P24, P25, P26, P27, P28, P29, P30, P31;
  wire [31:0] O0, O1, O2, O3, O4, O5, O6, O7, O8, O9, O10, O11, O12, O13, O14, O15, O16, O17, O18, O19, O20,
       O21, O22, O23, O24, O25, O26, O27, O28, O29, O30, O31;

  // Probe on out_12
  Demultiplexer #(.select(5)) demultiplexer_1 (
    .out0(demultiplexer_1_out0), .out1(P1), .out2(P2), .out3(P3), .out4(P4), .out5(P5), .out6(P6), .out7(P7),
    .out8(P8), .out9(P9), .out10(P10), .out11(P11), .out12(P12), .out13(P13), .out14(P14), .out15(P15),
    .out16(P16), .out17(P17), .out18(P18), .out19(P19), .out20(P20), .out21(P21), .out22(P22), .out23(P23),
    .out24(P24), .out25(P25), .out26(P26), .out27(P27), .out28(P28), .out29(P29), .out30(P30), .out31(P31),
    .in(RegWrite), .sel(out_12));  // open: en
  Multiplexer #(.width(5)) multiplexer_1 (.in0(A2), .in1(ins15_11), .out(out_12), .sel(RegDst));  // open: en
  Register #(.width(32)) _0 (.D(WD3), .en(1'b0), .Q(O0), .clk(CLK));  // open: clr
  Register #(.width(32)) _0_2 (.D(WD3), .en(P8), .Q(O8), .clk(CLK), .clr(in_9));
  Register #(.width(32)) _0_3 (.D(WD3), .en(P16), .Q(O16), .clk(CLK), .clr(in_9));
  Register #(.width(32)) _0_4 (.D(WD3), .en(P24), .Q(O24), .clk(CLK), .clr(in_9));
  Register #(.width(32)) _1 (.D(WD3), .en(P1), .Q(O1), .clk(CLK), .clr(in_9));
  Register #(.width(32)) _1_2 (.D(WD3), .en(P9), .Q(O9), .clk(CLK), .clr(in_9));
  Register #(.width(32)) _1_3 (.D(WD3), .en(P17), .Q(O17), .clk(CLK), .clr(in_9));
  Register #(.width(32)) _1_4 (.D(WD3), .en(P25), .Q(O25), .clk(CLK), .clr(in_9));
  Register #(.width(32)) _2 (.D(WD3), .en(P2), .Q(O2), .clk(CLK), .clr(in_9));
  Register #(.width(32)) _2_2 (.D(WD3), .en(P10), .Q(O10), .clk(CLK), .clr(in_9));
  Register #(.width(32)) _2_3 (.D(WD3), .en(P18), .Q(O18), .clk(CLK), .clr(in_9));
  Register #(.width(32)) _2_4 (.D(WD3), .en(P26), .Q(O26), .clk(CLK), .clr(in_9));
  Register #(.width(32)) _3 (.D(WD3), .en(P3), .Q(O3), .clk(CLK), .clr(in_9));
  Register #(.width(32)) _3_2 (.D(WD3), .en(P11), .Q(O11), .clk(CLK), .clr(in_9));
  Register #(.width(32)) _3_3 (.D(WD3), .en(P19), .Q(O19), .clk(CLK), .clr(in_9));
  Register #(.width(32)) _3_4 (.D(WD3), .en(P27), .Q(O27), .clk(CLK), .clr(in_9));
  Register #(.width(32)) _4 (.D(WD3), .en(P4), .Q(O4), .clk(CLK), .clr(in_9));
  Register #(.width(32)) _4_2 (.D(WD3), .en(P12), .Q(O12), .clk(CLK), .clr(in_9));
  Register #(.width(32)) _4_3 (.D(WD3), .en(P20), .Q(O20), .clk(CLK), .clr(in_9));
  Register #(.width(32)) _4_4 (.D(WD3), .en(P28), .Q(O28), .clk(CLK), .clr(in_9));
  Register #(.width(32)) _5 (.D(WD3), .en(P5), .Q(O5), .clk(CLK), .clr(in_9));
  Register #(.width(32)) _5_2 (.D(WD3), .en(P13), .Q(O13), .clk(CLK), .clr(in_9));
  Register #(.width(32)) _5_3 (.D(WD3), .en(P21), .Q(O21), .clk(CLK), .clr(in_9));
  Register #(.width(32)) _5_4 (.D(WD3), .en(P29), .Q(O29), .clk(CLK), .clr(in_9));
  Register #(.width(32)) _6 (.D(WD3), .en(P6), .Q(O6), .clk(CLK), .clr(in_9));
  Register #(.width(32)) _6_2 (.D(WD3), .en(P14), .Q(O14), .clk(CLK), .clr(in_9));
  Register #(.width(32)) _6_3 (.D(WD3), .en(P22), .Q(O22), .clk(CLK), .clr(in_9));
  Register #(.width(32)) _6_4 (.D(WD3), .en(P30), .Q(O30), .clk(CLK), .clr(in_9));
  Register #(.width(32)) _7 (.D(WD3), .en(P31), .Q(O31), .clk(CLK), .clr(in_9));
  Register #(.width(32)) _7_2 (.D(WD3), .en(P7), .Q(O7), .clk(CLK), .clr(in_9));
  Register #(.width(32)) _7_3 (.D(WD3), .en(P15), .Q(O15), .clk(CLK), .clr(in_9));
  Register #(.width(32)) _7_4 (.D(WD3), .en(P23), .Q(O23), .clk(CLK), .clr(in_9));
  Multiplexer #(.select(5), .width(32)) multiplexer_2 (
    .in0(O0), .in1(O1), .in2(O2), .in3(O3), .in4(O4), .in5(O5), .in6(O6), .in7(O7), .in8(O8), .in9(O9),
    .in10(O10), .in11(O11), .in12(O12), .in13(O13), .in14(O14), .in15(O15), .in16(O16), .in17(O17),
    .in18(O18), .in19(O19), .in20(O20), .in21(O21), .in22(O22), .in23(O23), .in24(O24), .in25(O25),
    .in26(O26), .in27(O27), .in28(O28), .in29(O29), .in30(O30), .in31(O31), .out(RD1), .sel(A1));  // open: en
  Multiplexer #(.select(5), .width(32)) multiplexer_3 (
    .in0(O0), .in1(O1), .in2(O2), .in3(O3), .in4(O4), .in5(O5), .in6(O6), .in7(O7), .in8(O8), .in9(O9),
    .in10(O10), .in11(O11), .in12(O12), .in13(O13), .in14(O14), .in15(O15), .in16(O16), .in17(O17),
    .in18(O18), .in19(O19), .in20(O20), .in21(O21), .in22(O22), .in23(O23), .in24(O24), .in25(O25),
    .in26(O26), .in27(O27), .in28(O28), .in29(O29), .in30(O30), .in31(O31), .out(RD2), .sel(A2));  // open: en

  // Other names for the same wires on the sheet: A3[4:0] = out_12; reset = in_9
endmodule

module control (
  input  op5,
  input  op4,
  input  op3,
  input  op2,
  input  op1,
  input  op0,
  input  ins1,
  input  ins0,
  output ALUctr1,
  output ALUctr0,
  output RegDst,
  output ALUSrc,
  output MemtoReg,
  output RegWrite,
  output Memwrite,
  output nPC_sel,
  output ExtOp
);

  wire addu_out, beq_out, lui_out, lw_out, not_1_out, not_2_out, not_3_out, not_4_out, not_5_out, not_6_out,
       not_7_out, ori_out, subu_out, sw_out;

  not not_1 (not_1_out, op5);
  not not_2 (not_2_out, op3);
  not not_3 (not_3_out, op4);
  not not_4 (not_4_out, op1);
  not not_5 (not_5_out, op2);
  not not_6 (not_6_out, ins1);
  not not_7 (not_7_out, op0);
  and addu (addu_out, not_1_out, not_3_out, not_2_out, not_5_out, not_4_out, not_7_out, not_6_out, ins0);
  and subu (subu_out, ins0, not_1_out, not_3_out, not_2_out, not_5_out, not_4_out, not_7_out, ins1);
  and ori (ori_out, not_1_out, not_3_out, op3, op2, not_4_out, op0);
  and lw (lw_out, op5, not_3_out, not_2_out, not_5_out, op1, op0);
  and sw (sw_out, op5, not_3_out, op3, not_5_out, op1, op0);
  and beq (beq_out, not_1_out, not_3_out, not_2_out, op2, not_4_out, not_7_out);
  and lui (lui_out, not_1_out, not_3_out, op3, op2, op1, op0);
  or u_RegDst (RegDst, addu_out, subu_out);
  buf u_MemtoReg (MemtoReg, lw_out);  // OR_Gate
  or u_ALUSrc (ALUSrc, ori_out, lw_out, sw_out, lui_out);
  or u_RegWrite (RegWrite, addu_out, subu_out, ori_out, lw_out, lui_out);
  buf u_Memwrite (Memwrite, sw_out);  // OR_Gate
  buf u_nPC_sel (nPC_sel, beq_out);  // OR_Gate
  or u_ExtOp (ExtOp, lw_out, sw_out, beq_out, lui_out);
  get_ALUctr get_aluctr_1 (
    .o6(addu_out), .o5(subu_out), .o4(ori_out), .o3(lw_out), .o2(sw_out), .o1(beq_out), .o0(lui_out),
    .ctr1(ALUctr1), .ctr0(ALUctr0));
endmodule

module get_ALUctr (
  input  o6,
  input  o5,
  input  o4,
  input  o3,
  input  o2,
  input  o1,
  input  o0,
  output ctr1,
  output ctr0
);

  wire not_1_out, not_2_out, not_3_out, not_4_out, not_5_out, not_6_out, not_7_out, not_8_out, not_9_out;

  not not_1 (not_1_out, o6);
  not not_2 (not_2_out, o5);
  not not_3 (not_3_out, o3);
  not not_4 (not_4_out, o2);
  not not_5 (not_5_out, o1);
  not not_6 (not_6_out, o6);
  not not_7 (not_7_out, o4);
  not not_8 (not_8_out, o3);
  not not_9 (not_9_out, o2);
  and and_1 (ctr1, not_1_out, not_2_out, not_3_out, not_4_out, not_5_out);
  and and_2 (ctr0, not_6_out, not_7_out, not_8_out, not_9_out);
endmodule

// ext
module sign_ex (
  input  in_1,
  output [31:0] out_2
);


  assign out_2 = {32{in_1}};
endmodule

module ALU (
  input  [1:0] ALUctr,
  input  [31:0] SrcA,
  input  [31:0] SrcB,
  output ZERO,
  output [31:0] ALUResult
);

  wire or_2_out;
  wire [31:0] adder_1_out, or_1_out, subtractor_1_out;

  Adder #(.width(32)) adder_1 (.a(SrcA), .b(SrcB), .out(adder_1_out));  // open: cin, cout
  Subtractor #(.width(32)) subtractor_1 (.a(SrcA), .b(SrcB), .out(subtractor_1_out));  // open: bin, bout
  assign or_1_out = SrcA | SrcB;  // OR_Gate or_1, 32 bits wide
  Multiplexer #(.select(2), .width(32)) multiplexer_1 (
    .in0(adder_1_out), .in1(subtractor_1_out), .in2(or_1_out), .in3({SrcB[15:0], {16{1'b0}}}),
    .out(ALUResult), .sel(ALUctr));  // open: en
  or or_2 (or_2_out, ALUResult[0], ALUResult[1], ALUResult[2], ALUResult[3], ALUResult[4], ALUResult[5], ALUResult[6], ALUResult[7], ALUResult[8], ALUResult[9], ALUResult[10], ALUResult[11], ALUResult[12], ALUResult[13], ALUResult[14], ALUResult[15], ALUResult[16], ALUResult[17], ALUResult[18], ALUResult[19], ALUResult[20], ALUResult[21], ALUResult[22], ALUResult[23], ALUResult[24], ALUResult[25], ALUResult[26], ALUResult[27], ALUResult[28], ALUResult[29], ALUResult[30], ALUResult[31]);
  not not_1 (ZERO, or_2_out);

  // Other names for the same wires on the sheet: ctr[1:0] = ALUctr
endmodule

module DM (
  input  MemWrite,
  input  [31:0] ALUResult,
  input  CLK,
  input  [31:0] WriteData,
  input  reset,
  output [4:0] MemAddr,
  output [31:0] ReadData
);

  RAM #(.addrWidth(5), .dataWidth(32), .bus("separate")) ram_1 (
    .addr(ALUResult[6:2]), .din(WriteData), .data(ReadData), .str(MemWrite), .clk(CLK), .clr(reset));  // open: sel, ld

  assign MemAddr = ALUResult[6:2];
endmodule

module EXT (
  input  ExtOp,
  input  [15:0] imm,
  output [31:0] Ext_num
);

  Multiplexer #(.width(32)) multiplexer_1 (
    .in0({{16{1'b0}}, imm}), .in1({{17{imm[15]}}, imm[14:0]}), .out(Ext_num), .sel(ExtOp));  // open: en
endmodule

module shift_2 (
  input  [31:0] in_1,
  output [29:0] out_2
);


  assign out_2 = in_1[29:0];
endmodule
