// Logisim project single_cpu_plus.circ as structural Verilog: 8 circuits, main circuit main
module main (
  input  Reset,
  output [31:0] Instr,
  output RegWrite,
  output [4:0] RegAddr,
  output [31:0] RegData,
  output MemWrite,
  output [4:0] MemAddr,
  output [31:0] MemData
);

  wire ALU_zero, ALUSrc, clk, control_npc_sel, ifu_1_ins0, ifu_1_ins1, ifu_1_ins2, ifu_1_ins3, ifu_1_ins4,
       ifu_1_ins5, ifu_1_op0, ifu_1_op1, ifu_1_op2, ifu_1_op3, ifu_1_op4, ifu_1_op5, load_u, PCSrc;
  wire [1:0] ExtOp, j_src, j_zero, MemtoReg, RegDst, word_bit;
  wire [2:0] ALUctr;
  wire [4:0] in_11_15, in_16_20, in_21_25;
  wire [15:0] imm;
  wire [29:0] adder_2_out, multiplexer_1_out, PCBranch, PLUS1, register_1_q, shift_2_1_out_2, shift_2_2_out_2;
  wire [31:0] ALU_aluresult, DM_readdata, EXT_ext_num, multiplexer_2_out, PLUS2, RD_1;

  Clock clock_1 (.out(clk));
  Register #(.width(30)) register_1 (.D(multiplexer_1_out), .Q(register_1_q), .clk(clk), .clr(Reset));  // open: en
  Multiplexer #(.width(30)) multiplexer_1 (
    .in0(PLUS1), .in1(PCBranch), .out(multiplexer_1_out), .sel(PCSrc));  // open: en
  Adder #(.width(30)) adder_1 (.a(register_1_q), .b(30'h1), .out(PLUS1));  // open: cin, cout
  IFU ifu_1 (
    .PC(register_1_q), .instruction(Instr), .ins0(ifu_1_ins0), .ins1(ifu_1_ins1), .ins3(ifu_1_ins3),
    .op0(ifu_1_op0), .op1(ifu_1_op1), .op2(ifu_1_op2), .op3(ifu_1_op3), .op4(ifu_1_op4), .op5(ifu_1_op5),
    .in_21_25(in_21_25), .in_16_20(in_16_20), .in_11_15(in_11_15), .imm(imm), .ins2(ifu_1_ins2),
    .ins4(ifu_1_ins4), .ins5(ifu_1_ins5));
  assign PLUS2 = {{2{PLUS1[29]}}, PLUS1};  // Bit_Extender bit_extender_1
  control control (
    .op5(ifu_1_op5), .op4(ifu_1_op4), .op3(ifu_1_op3), .op2(ifu_1_op2), .op1(ifu_1_op1), .op0(ifu_1_op0),
    .ins1(ifu_1_ins1), .ALUSrc(ALUSrc), .RegWrite(RegWrite), .Memwrite(MemWrite), .nPC_sel(control_npc_sel),
    .ExtOp(ExtOp), .ins0(ifu_1_ins0), .word_bit(word_bit), .ins3(ifu_1_ins3), .j_src(j_src),
    .ins2(ifu_1_ins2), .ins4(ifu_1_ins4), .ins5(ifu_1_ins5), .RegDst(RegDst), .MemtoReg(MemtoReg),
    .load_u(load_u), .j_zero(j_zero), .ALU_ctr(ALUctr));
  EXT EXT (.ExtOp(ExtOp), .imm(imm), .jal_offset({in_21_25, in_16_20, imm}), .Ext_num(EXT_ext_num));
  shift_2 shift_2_1 (.in_1(EXT_ext_num), .out_2(shift_2_1_out_2));
  GPR GRF (
    .CLK(clk), .RegDst(RegDst), .A1(in_21_25), .A2(in_16_20), .ins15_11(in_11_15), .WD3(RegData),
    .RegWrite(RegWrite), .reset(Reset), .RD1(RD_1), .RD2(MemData), .out_11(RegAddr));
  Multiplexer #(.width(32)) multiplexer_2 (
    .in0(MemData), .in1(EXT_ext_num), .out(multiplexer_2_out), .sel(ALUSrc));  // open: en
  and and_1 (PCSrc, control_npc_sel, ALU_zero);
  ALU ALU (
    .ALUctr(ALUctr), .SrcA(RD_1), .SrcB(multiplexer_2_out), .in_4(j_zero), .ZERO(ALU_zero),
    .ALUResult(ALU_aluresult));
  Adder #(.width(30)) adder_2 (.a(shift_2_1_out_2), .b(PLUS1), .out(adder_2_out));  // open: cin, cout
  shift_2 shift_2_2 (.in_1(RD_1), .out_2(shift_2_2_out_2));
  Multiplexer #(.select(2), .width(30)) multiplexer_3 (
    .in0(adder_2_out), .in1(shift_2_1_out_2), .in2(shift_2_2_out_2), .out(PCBranch), .sel(j_src));  // open: in3, en
  DM DM (
    .MemWrite(MemWrite), .ALUResult(ALU_aluresult), .WriteData(MemData), .ReadData(DM_readdata), .CLK(clk),
    .reset(Reset), .MemAddr(MemAddr), .word_bit(word_bit), .load_u(load_u));
  Multiplexer #(.select(2), .width(32)) multiplexer_4 (
    .in0(ALU_aluresult), .in1(DM_readdata), .in2(PLUS2), .out(RegData), .sel(MemtoReg));  // open: in3, en
endmodule

module IFU (
  input  [29:0] PC,
  output [31:0] instruction,
  output ins0,
  output ins1,
  output ins2,
  output ins3,
  output ins4,
  output ins5,
  output op0,
  output op1,
  output op2,
  output op3,
  output op4,
  output op5,
  output [4:0] in_21_25,
  output [4:0] in_16_20,
  output [4:0] in_11_15,
  output [15:0] imm
);

  ROM #(.addrWidth(5), .dataWidth(32)) rom_1 (
    .addr(PC[4:0]), .data({instruction[31:26], in_21_25, in_16_20, imm}));  // open: sel

  assign in_11_15 = imm[15:11];
  assign ins0 = imm[0];
  assign ins1 = imm[1];
  assign ins2 = imm[2];
  assign ins3 = imm[3];
  assign ins4 = imm[4];
  assign ins5 = imm[5];
  assign instruction[25:0] = {in_21_25, in_16_20, imm};
  assign op0 = instruction[26];
  assign op1 = instruction[27];
  assign op2 = instruction[28];
  assign op3 = instruction[29];
  assign op4 = instruction[30];
  assign op5 = instruction[31];
endmodule

module GPR (
  input  CLK,
  input  [1:0] RegDst,
  input  [4:0] A1,
  input  [4:0] A2,
  input  [4:0] ins15_11,
  input  [31:0] WD3,
  input  RegWrite,
  input  reset,
  output [31:0] RD1,
  output [31:0] RD2,
  output [4:0] out_11
);

  wire demultiplexer_1_out0, P1, P2, P3, P4, P5, P6, P7, P8, P9, P10, P11, P12, P13, P14, P15, P16, P17, P18,
       P19, P20, P21, P22, P23, P24, P25, P26, P27, P28, P29, P30, P31;
  wire [31:0] O0, O1, O2, O3, O4, O5, O6, O7, O8, O9, O10, O11, O12, O13, O14, O15, O16, O17, O18, O19, O20,
       O21, O22, O23, O24, O25, O26, O27, O28, O29, O30, O31;

  // Probe on out_11
  Multiplexer #(.select(2), .width(5)) multiplexer_1 (
    .in0(A2), .in1(ins15_11), .in2({5{1'b1}}), .out(out_11), .sel(RegDst));  // open: in3, en
  Demultiplexer #(.select(5)) demultiplexer_1 (
    .out0(demultiplexer_1_out0), .out1(P1), .out2(P2), .out3(P3), .out4(P4), .out5(P5), .out6(P6), .out7(P7),
    .out8(P8), .out9(P9), .out10(P10), .out11(P11), .out12(P12), .out13(P13), .out14(P14), .out15(P15),
    .out16(P16), .out17(P17), .out18(P18), .out19(P19), .out20(P20), .out21(P21), .out22(P22), .out23(P23),
    .out24(P24), .out25(P25), .out26(P26), .out27(P27), .out28(P28), .out29(P29), .out30(P30), .out31(P31),
    .in(RegWrite), .sel(out_11));  // open: en
  Register #(.width(32)) _0 (.D(WD3), .en(1'b0), .Q(O0), .clk(CLK));  // open: clr
  Register #(.width(32)) _0_2 (.D(WD3), .en(P8), .Q(O8), .clk(CLK), .clr(reset));
  Register #(.width(32)) _0_3 (.D(WD3), .en(P16), .Q(O16), .clk(CLK), .clr(reset));
  Register #(.width(32)) _0_4 (.D(WD3), .en(P24), .Q(O24), .clk(CLK), .clr(reset));
  Register #(.width(32)) _1 (.D(WD3), .en(P1), .Q(O1), .clk(CLK), .clr(reset));
  Register #(.width(32)) _1_2 (.D(WD3), .en(P9), .Q(O9), .clk(CLK), .clr(reset));
  Register #(.width(32)) _1_3 (.D(WD3), .en(P17), .Q(O17), .clk(CLK), .clr(reset));
  Register #(.width(32)) _1_4 (.D(WD3), .en(P25), .Q(O25), .clk(CLK), .clr(reset));
  Register #(.width(32)) _2 (.D(WD3), .en(P2), .Q(O2), .clk(CLK), .clr(reset));
  Register #(.width(32)) _2_2 (.D(WD3), .en(P10), .Q(O10), .clk(CLK), .clr(reset));
  Register #(.width(32)) _2_3 (.D(WD3), .en(P18), .Q(O18), .clk(CLK), .clr(reset));
  Register #(.width(32)) _2_4 (.D(WD3), .en(P26), .Q(O26), .clk(CLK), .clr(reset));
  Register #(.width(32)) _3 (.D(WD3), .en(P3), .Q(O3), .clk(CLK), .clr(reset));
  Register #(.width(32)) _3_2 (.D(WD3), .en(P11), .Q(O11), .clk(CLK), .clr(reset));
  Register #(.width(32)) _3_3 (.D(WD3), .en(P19), .Q(O19), .clk(CLK), .clr(reset));
  Register #(.width(32)) _3_4 (.D(WD3), .en(P27), .Q(O27), .clk(CLK), .clr(reset));
  Register #(.width(32)) _4 (.D(WD3), .en(P4), .Q(O4), .clk(CLK), .clr(reset));
  Register #(.width(32)) _4_2 (.D(WD3), .en(P12), .Q(O12), .clk(CLK), .clr(reset));
  Register #(.width(32)) _4_3 (.D(WD3), .en(P20), .Q(O20), .clk(CLK), .clr(reset));
  Register #(.width(32)) _4_4 (.D(WD3), .en(P28), .Q(O28), .clk(CLK), .clr(reset));
  Register #(.width(32)) _5 (.D(WD3), .en(P5), .Q(O5), .clk(CLK), .clr(reset));
  Register #(.width(32)) _5_2 (.D(WD3), .en(P13), .Q(O13), .clk(CLK), .clr(reset));
  Register #(.width(32)) _5_3 (.D(WD3), .en(P21), .Q(O21), .clk(CLK), .clr(reset));
  Register #(.width(32)) _5_4 (.D(WD3), .en(P29), .Q(O29), .clk(CLK), .clr(reset));
  Register #(.width(32)) _6 (.D(WD3), .en(P6), .Q(O6), .clk(CLK), .clr(reset));
  Register #(.width(32)) _6_2 (.D(WD3), .en(P14), .Q(O14), .clk(CLK), .clr(reset));
  Register #(.width(32)) _6_3 (.D(WD3), .en(P22), .Q(O22), .clk(CLK), .clr(reset));
  Register #(.width(32)) _6_4 (.D(WD3), .en(P30), .Q(O30), .clk(CLK), .clr(reset));
  Register #(.width(32)) _7 (.D(WD3), .en(P31), .Q(O31), .clk(CLK), .clr(reset));
  Register #(.width(32)) _7_2 (.D(WD3), .en(P7), .Q(O7), .clk(CLK), .clr(reset));
  Register #(.width(32)) _7_3 (.D(WD3), .en(P15), .Q(O15), .clk(CLK), .clr(reset));
  Register #(.width(32)) _7_4 (.D(WD3), .en(P23), .Q(O23), .clk(CLK), .clr(reset));
  Multiplexer #(.select(5), .width(32)) multiplexer_2 (
    .in0(O0), .in1(O1), .in2(O2), .in3(O3), .in4(O4), .in5(O5), .in6(O6), .in7(O7), .in8(O8), .in9(O9),
    .in10(O10), .in11(O11), .in12(O12), .in13(O13), .in14(O14), .in15(O15), .in16(O16), .in17(O17),
    .in18(O18), .in19(O19), .in20(O20), .in21(O21), .in22(O22), .in23(O23), .in24(O24), .in25(O25),
    .in26(O26), .in27(O27), .in28(O28), .in29(O29), .in30(O30), .in31(O31), .out(RD1), .sel(A1));  // open: en
  Multiplexer #(.select(5), .width(32)) multiplexer_3 (
    .in0(O0), .in1(O1), .in2(O2), .in3(O3), .in4(O4), .in5(O5), .in6(O6), .in7(O7), .in8(O8), .in9(O9),
    .in10(O10), .in11(O11), .in12(O12), .in13(O13), .in14(O14), .in15(O15), .in16(O16), .in17(O17),
    .in18(O18), .in19(O19), .in20(O20), .in21(O21), .in22(O22), .in23(O23), .in24(O24), .in25(O25),
    .in26(O26), .in27(O27), .in28(O28), .in29(O29), .in30(O30), .in31(O31), .out(RD2), .sel(A2));  // open: en

  // Other names for the same wires on the sheet: A3[4:0] = out_11
endmodule

module control (
  input  op5,
  input  op4,
  input  op3,
  input  op2,
  input  op1,
  input  op0,
  input  ins5,
  input  ins4,
  input  ins3,
  input  ins2,
  input  ins1,
  input  ins0,
  output RegWrite,
  output Memwrite,
  output nPC_sel,
  output ALUSrc,
  output load_u,
  output [1:0] RegDst,
  output [1:0] MemtoReg,
  output [1:0] ExtOp,
  output [1:0] word_bit,
  output [1:0] j_src,
  output [1:0] j_zero,
  output [2:0] ALU_ctr
);

  wire addu_out, beq_out, jal_out, jr_out, lb_out, lbu_out, lh_out, lhu_out, lui_out, lw_out, not_1_out,
       not_2_out, not_3_out, not_4_out, not_5_out, not_6_out, not_7_out, not_8_out, not_9_out, not_10_out,
       not_11_out, not_12_out, ori_out, sb_out, sh_out, subu_out, sw_out, xor_out, xori_out;

  not not_1 (not_1_out, op5);
  not not_2 (not_2_out, op4);
  not not_3 (not_3_out, op3);
  not not_4 (not_4_out, op2);
  not not_5 (not_5_out, op1);
  not not_6 (not_6_out, op0);
  not not_7 (not_7_out, ins5);
  not not_8 (not_8_out, ins4);
  not not_9 (not_9_out, ins2);
  not not_10 (not_10_out, ins3);
  not not_11 (not_11_out, ins1);
  not not_12 (not_12_out, ins0);
  and addu (addu_out, not_8_out, ins5, not_1_out, not_2_out, not_3_out, not_4_out, not_5_out, not_6_out, not_11_out, ins0, not_9_out);
  and ori (ori_out, not_1_out, not_2_out, op3, op2, not_5_out, op0);
  and lw (lw_out, op5, not_2_out, not_3_out, not_4_out, op1, op0);
  and sw (sw_out, op5, not_2_out, op3, not_4_out, op1, op0);
  and beq (beq_out, not_1_out, not_2_out, not_3_out, op2, not_5_out, not_6_out);
  and lui (lui_out, not_1_out, not_2_out, op3, op2, op1, op0);
  and xori (xori_out, not_1_out, not_2_out, op3, op2, op1, not_6_out);
  and lh (lh_out, op5, not_2_out, not_3_out, not_4_out, not_5_out, op0);
  and sb (sb_out, op5, not_2_out, op3, not_4_out, not_5_out, not_6_out);
  and jal (jal_out, not_1_out, not_2_out, not_3_out, not_4_out, op1, op0);
  and jr (jr_out, not_1_out, not_2_out, not_3_out, not_4_out, not_5_out, not_6_out, ins3, not_11_out);
  and lbu (lbu_out, op5, not_2_out, not_3_out, op2, not_5_out, not_6_out);
  and lhu (lhu_out, op5, not_2_out, not_3_out, op2, not_5_out, op0);
  and lb (lb_out, op5, not_2_out, not_3_out, not_4_out, not_5_out, not_6_out);
  and sh (sh_out, op5, not_2_out, op3, not_4_out, not_5_out, op0);
  and \xor  (xor_out, not_1_out, not_2_out, not_3_out, not_4_out, not_5_out, not_6_out, ins5, not_8_out, not_10_out, ins2, ins1, not_12_out);
  and subu (subu_out, ins0, not_1_out, not_2_out, not_3_out, not_4_out, not_5_out, not_6_out, ins1, ins5);
  buf u_RegDst (RegDst[1], jal_out);  // OR_Gate
  or RegDst_2 (RegDst[0], addu_out, subu_out, xor_out);
  or u_ALUSrc (ALUSrc, lb_out, ori_out, lw_out, sw_out, lui_out, lbu_out, xori_out, lh_out, sb_out, lhu_out, sh_out);
  buf u_MemtoReg (MemtoReg[1], jal_out);  // OR_Gate
  or MemtoReg_2 (MemtoReg[0], lw_out, lh_out, lbu_out, lhu_out, lb_out);
  or u_RegWrite (RegWrite, lb_out, addu_out, subu_out, ori_out, lw_out, lui_out, xori_out, lh_out, jal_out, lbu_out, lhu_out, xor_out);
  or u_Memwrite (Memwrite, sw_out, sb_out, sh_out);
  or u_nPC_sel (nPC_sel, beq_out, jal_out, jr_out);
  buf u_ExtOp (ExtOp[1], jal_out);  // OR_Gate
  or ExtOp_2 (ExtOp[0], sh_out, lb_out, lw_out, sw_out, beq_out, lhu_out, lh_out, sb_out, lbu_out);
  or u_word_bit (word_bit[1], lbu_out, sb_out, lb_out);
  or word_bit_2 (word_bit[0], sh_out, lh_out, lhu_out);
  or u_load_u (load_u, lbu_out, lhu_out);
  buf j_src1 (j_src[1], jr_out);  // OR_Gate
  buf j_src0 (j_src[0], jal_out);  // OR_Gate
  or or_1 (ALU_ctr[2], xori_out, xor_out);
  or or_2 (ALU_ctr[1], lui_out, ori_out);
  or or_3 (ALU_ctr[0], subu_out, lui_out, beq_out);
  buf j_src1_2 (j_zero[1], 1'b0);  // OR_Gate
  buf j_src0_2 (j_zero[0], beq_out);  // OR_Gate
endmodule

module ALU (
  input  [2:0] ALUctr,
  input  [31:0] SrcA,
  input  [31:0] SrcB,
  input  [1:0] in_4,
  output ZERO,
  output [31:0] ALUResult
);

  wire comparator_1_eq;
  wire [31:0] adder_1_out, or_1_out, subtractor_1_out, xor_1_out;

  Adder #(.width(32)) adder_1 (.a(SrcA), .b(SrcB), .out(adder_1_out));  // open: cin, cout
  Subtractor #(.width(32)) subtractor_1 (.a(SrcA), .b(SrcB), .out(subtractor_1_out));  // open: bin, bout
  assign or_1_out = SrcA | SrcB;  // OR_Gate or_1, 32 bits wide
  assign xor_1_out = SrcA ^ SrcB;  // XOR_Gate xor_1, 32 bits wide
  Comparator #(.width(32)) comparator_1 (.a(SrcA), .b(SrcB), .eq(comparator_1_eq));  // open: gt, lt
  Multiplexer #(.select(3), .width(32)) multiplexer_1 (
    .in0(adder_1_out), .in1(subtractor_1_out), .in2(or_1_out), .in3({SrcB[15:0], {16{1'b0}}}),
    .in4(xor_1_out), .in5({32{1'b0}}), .in6({32{1'b0}}), .in7({32{1'b0}}), .out(ALUResult), .sel(ALUctr));  // open: en
  Multiplexer #(.select(2)) multiplexer_2 (
    .in0(1'b1), .in1(comparator_1_eq), .out(ZERO), .sel(in_4));  // open: in2, in3, en

  // Other names for the same wires on the sheet: ctr[2:0] = ALUctr; j_zero[1:0] = in_4
endmodule

module DM (
  input  MemWrite,
  input  [31:0] ALUResult,
  input  CLK,
  input  [31:0] WriteData,
  input  reset,
  input  [1:0] word_bit,
  input  load_u,
  output [4:0] MemAddr,
  output [31:0] ReadData
);

  wire [7:0] dm_0, dm_1, dm_2, dm_3;
  wire [15:0] ram_1_data, ram_1_data_2;
  wire [31:0] bit_extender_1_out, bit_extender_2_out, bit_extender_3_out, bit_extender_4_out,
       bit_extender_5_out, bit_extender_6_out, bit_extender_7_out, bit_extender_8_out, bit_extender_9_out,
       bit_extender_10_out, bit_extender_11_out, bit_extender_12_out, multiplexer_1_out, multiplexer_2_out,
       multiplexer_3_out, multiplexer_4_out, multiplexer_5_out, multiplexer_6_out, multiplexer_7_out,
       multiplexer_8_out, multiplexer_9_out, multiplexer_10_out, multiplexer_11_out;

  Multiplexer #(.width(32)) multiplexer_1 (
    .in0({dm_3, dm_2, WriteData[15:0]}), .in1({WriteData[15:0], dm_1, dm_0}), .out(multiplexer_1_out),
    .sel(ALUResult[1]));  // open: en
  Multiplexer #(.select(2), .width(32)) multiplexer_2 (
    .in0({dm_3, dm_2, dm_1, WriteData[7:0]}), .in1({dm_3, dm_2, WriteData[7:0], dm_0}),
    .in2({dm_3, WriteData[7:0], dm_1, dm_0}), .in3({WriteData[7:0], dm_2, dm_1, dm_0}),
    .out(multiplexer_2_out), .sel(ALUResult[1:0]));  // open: en
  Multiplexer #(.select(2), .width(32)) multiplexer_3 (
    .in0(WriteData), .in1(multiplexer_1_out), .in2(multiplexer_2_out), .out(multiplexer_3_out), .sel(word_bit));  // open: in3, en
  assign bit_extender_1_out = {{24{ram_1_data[7]}}, ram_1_data[7:0]};  // Bit_Extender bit_extender_1
  assign bit_extender_2_out = {{24{1'b0}}, ram_1_data[7:0]};  // Bit_Extender bit_extender_2
  assign bit_extender_3_out = {{24{ram_1_data[15]}}, ram_1_data[15:8]};  // Bit_Extender bit_extender_3
  assign bit_extender_4_out = {{24{1'b0}}, ram_1_data[15:8]};  // Bit_Extender bit_extender_4
  assign bit_extender_5_out = {{24{ram_1_data_2[7]}}, ram_1_data_2[7:0]};  // Bit_Extender bit_extender_5
  assign bit_extender_6_out = {{24{1'b0}}, ram_1_data_2[7:0]};  // Bit_Extender bit_extender_6
  assign bit_extender_7_out = {{24{ram_1_data_2[15]}}, ram_1_data_2[15:8]};  // Bit_Extender bit_extender_7
  assign bit_extender_8_out = {{24{1'b0}}, ram_1_data_2[15:8]};  // Bit_Extender bit_extender_8
  RAM #(.addrWidth(5), .dataWidth(32), .bus("separate")) ram_1 (
    .addr(ALUResult[6:2]), .din(multiplexer_3_out), .data({ram_1_data_2, ram_1_data}), .str(MemWrite),
    .clk(CLK), .clr(reset));  // open: sel, ld
  assign bit_extender_9_out = {{16{ram_1_data[15]}}, ram_1_data};  // Bit_Extender bit_extender_9
  assign bit_extender_10_out = {{16{1'b0}}, ram_1_data};  // Bit_Extender bit_extender_10
  assign bit_extender_11_out = {{16{ram_1_data_2[15]}}, ram_1_data_2};  // Bit_Extender bit_extender_11
  assign bit_extender_12_out = {{16{1'b0}}, ram_1_data_2};  // Bit_Extender bit_extender_12
  Multiplexer #(.width(32)) multiplexer_4 (
    .in0(bit_extender_1_out), .in1(bit_extender_2_out), .out(multiplexer_4_out), .sel(load_u));  // open: en
  Multiplexer #(.width(32)) multiplexer_5 (
    .in0(bit_extender_3_out), .in1(bit_extender_4_out), .out(multiplexer_5_out), .sel(load_u));  // open: en
  Multiplexer #(.width(32)) multiplexer_6 (
    .in0(bit_extender_5_out), .in1(bit_extender_6_out), .out(multiplexer_6_out), .sel(load_u));  // open: en
  Multiplexer #(.width(32)) multiplexer_7 (
    .in0(bit_extender_7_out), .in1(bit_extender_8_out), .out(multiplexer_7_out), .sel(load_u));  // open: en
  Multiplexer #(.width(32)) multiplexer_8 (
    .in0(bit_extender_9_out), .in1(bit_extender_10_out), .out(multiplexer_8_out), .sel(load_u));  // open: en
  Multiplexer #(.width(32)) multiplexer_9 (
    .in0(bit_extender_11_out), .out(multiplexer_9_out), .sel(load_u));  // open: in1, en
  Multiplexer #(.select(2), .width(32)) multiplexer_10 (
    .in0(multiplexer_4_out), .in1(multiplexer_5_out), .in2(multiplexer_6_out), .in3(multiplexer_7_out),
    .out(multiplexer_10_out), .sel(ALUResult[1:0]));  // open: en
  Multiplexer #(.width(32)) multiplexer_11 (
    .in0(multiplexer_8_out), .in1(multiplexer_9_out), .out(multiplexer_11_out), .sel(ALUResult[1]));  // open: en
  Multiplexer #(.select(2), .width(32)) multiplexer_12 (
    .in0({ram_1_data_2, ram_1_data}), .in1(multiplexer_11_out), .in2(multiplexer_10_out), .out(ReadData),
    .sel(word_bit));  // open: in3, en

  assign MemAddr = ALUResult[6:2];

  // Other names for the same wires on the sheet: res_10[1:0] = ALUResult[1:0]; res_1 = ALUResult[1]
endmodule

module EXT (
  input  [1:0] ExtOp,
  input  [15:0] imm,
  input  [25:0] jal_offset,
  output [31:0] Ext_num
);

  Multiplexer #(.select(2), .width(32)) multiplexer_1 (
    .in0({{16{1'b0}}, imm}), .in1({{17{imm[15]}}, imm[14:0]}), .in2({2'b00, jal_offset, 4'b0000}),
    .out(Ext_num), .sel(ExtOp));  // open: in3, en
endmodule

// shift2
module shift_2 (
  input  [31:0] in_1,
  output [29:0] out_2
);


  assign out_2 = in_1[29:0];
endmodule
